# Fritzing sketch Ovah_v0.1_23_07_17 (saved by Fritzing 0.9.3b)
circuit board: 4.43919cm x 4.94cm
breadboards: 1

parts:
  C1 = Electrolytic Capacitor [capacitance=2.2µF package="100 mil [THT, electrolytic]"]
  U1_LM386 = LM386 [package=dip08]
  P2_A10kΩ = POT [package=pot_alpha_rv16af-20]
  P1_A10kΩ = POT [package=pot_alpha_rv16af-20]
  C2 = Electrolytic Capacitor [capacitance=10µF package="100 mil [THT, electrolytic]"]
  C3 = Electrolytic Capacitor [capacitance=100µF package="100 mil [THT, electrolytic]"]
  R1 = Resistor [tolerance=±5% resistance=10k package=THT]
  R2 = Resistor [tolerance=±5% resistance=220k package=THT]
  R3 = Resistor [tolerance=±5% resistance=100k package=THT]
  D1 = Rectifier Diode [part_number=1N4001 package="300 mil [THT]"]
  D2 = Rectifier Diode [part_number=1N4001 package="300 mil [THT]"]
  C4 = Ceramic Capacitor [capacitance=47nF package="100 mil [THT, multilayer]"]
  S2 = SPST Switch [package=switch-spdt]
  9V_DC = Battery block 9V
  J1 = female pin header, 2 pins [form="♀ (female)"]
  J2 = female pin header, 2 pins [form="♀ (female)"]

nets:
  N1: C1.-, U1_LM386.+IN
  Input: C1.+, J1.pin1
  N2: U1_LM386.GAIN, P1_A10kΩ.A, C2.+
  GND: U1_LM386.-IN, U1_LM386.V-, P2_A10kΩ.A, R1.Pin_0, D1.anode, D2.cathode, 9V_DC.-, J1.pin2, J2.pin2
  N3: U1_LM386.OUT, C3.+, C4.1, S2.O
  9V: U1_LM386.V+, 9V_DC.+
  Output: P2_A10kΩ.S, J2.pin1
  N4: P2_A10kΩ.E, R3.Pin_1
  N5: P1_A10kΩ.S, P1_A10kΩ.E, C2.-
  N6: C3.-, R2.Pin_0
  N7: R1.Pin_1, C4.0
  N8: R2.Pin_1, R3.Pin_0
  N9: D1.cathode, D2.anode, S2.P

notes:
  OvahDrive, Overdrive with LM386 Opamp and clipping diodes. The diodes can be any kind; whatever sounds better., v0.1
  Gain
  Level
  IN
  OUT
  Ovah v0.1
