# Fritzing sketch Ovah_v1.1_29_10_17 (saved by Fritzing 0.9.3b)
circuit board: 4.43919cm x 4.94cm
breadboards: 1

parts:
  C1 = Electrolytic Capacitor [capacitance=2.2µF package="100 mil [THT, electrolytic]"]
  U1_LM386 = LM386 [package=dip08]
  P2_A10kΩ = POT [package=pot_alpha_rv16af-20]
  P1_B10kΩ = POT [package=pot_alpha_rv16af-20]
  C2 = Electrolytic Capacitor [capacitance=10µF package="100 mil [THT, electrolytic]"]
  R1 = Resistor [tolerance=±5% resistance=10k package=THT]
  R2 = Resistor [tolerance=±5% resistance=200k package=THT]
  9V_DC = Battery block 9V
  J1 = female pin header, 2 pins [form="♀ (female)"]
  J2 = female pin header, 2 pins [form="♀ (female)"]
  D1 = Rectifier Diode [part_number=1N4001 package="300 mil [THT]"]
  C3 = Electrolytic Capacitor [capacitance=100µF package="200 mil [THT, electrolytic]"]
  C4 = Ceramic Capacitor [capacitance=47nF package="200 mil [THT, multilayer]"]

nets:
  N1: C1.-, U1_LM386.+IN
  Input: C1.+, J1.pin1
  N2: U1_LM386.GAIN, P1_B10kΩ.A, C2.+
  GND: U1_LM386.-IN, U1_LM386.V-, P2_A10kΩ.A, R1.Pin_0, 9V_DC.-, J1.pin2, J2.pin2
  N3: U1_LM386.OUT, C3.+, C4.1
  9V: U1_LM386.V+, D1.cathode
  Output: P2_A10kΩ.S, J2.pin1
  N4: P2_A10kΩ.E, R2.Pin_1
  N5: P1_B10kΩ.S, P1_B10kΩ.E, C2.-
  N6: R1.Pin_1, C4.0
  N7: R2.Pin_0, C3.-
  N8: 9V_DC.+, D1.anode

notes:
  OvahDrive, Overdrive with LM386 Opamp and clipping diodes. The diodes can be any kind; whatever sounds better., v1.1
  Gain
  Level
  IN
  OUT
  Ovah v1.1
